# Fritzing sketch Nitrox analyser narrow (saved by Fritzing 0.9.4)
circuit board: 2.9cm x 4.47998cm
perfboards: 1

parts:
  Nano = Arduino Nano (Rev3.0)
  ADS1115 = Adafruit ADS1115 16Bit I2C ADC [part_number="Adafruit #1085"]
  Button = Round Pushbutton
  J1 = SMA Antenna Connector RA 6mm pad spacing
  S1 = Toggle Switch spst [package=THT]
  VCC = Battery block 9V
  Screen = OLED 128x64 I2C Monochrome Display

nets:
  GND: Nano.GND, ADS1115.GND, Button.leg0, VCC.-, Screen.GND
  N1: Nano.D5, Button.leg1
  N2: Nano.VIN, S1.COM
  VDD: Nano.5V, ADS1115.VDD, Screen.VDD
  N3: Nano.A5, ADS1115.SCL, Screen.SCK
  N4: Nano.A4, ADS1115.SDA, Screen.SDA
  N5: ADS1115.AIN1, J1.SIGNAL
  N6: ADS1115.AIN0, J1.GND
  N7: S1.L1, VCC.+

notes:
  Oxygen Analyser v1
  O2 cell
  Design by Xavier Vrijdag
  + -
  JLCJLCJLCJLC

custom parts:
  Adafruit ADS1115 16Bit I2C ADC: For microcontrollers without an analog-to-digital converter or when you want a higher-precision ADC, the ADS1115 provides 16-bit precision at 860 samples/second over I2C. The chip can be configured as 4 single-ended input channels, or two differential channels. As a nice bonus, it even includes a programmable gain amplifier, up to x16, to help boost up smaller single/differential signals to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
  SMA Antenna Connector RA 6mm pad spacing: SMA RA Antenna Connector with 6mm pcb pad spacing.
  Toggle Switch spst: Toggle Switch single pole single throw
